# Fritzing sketch ESP32 y dht11 (saved by Fritzing 0.9.3b)
breadboards: 1

parts:
  E1 = ESP32-Cam
  Mod1 = KY-015 Temperature & Humidity Sensor Module [package="Breakout board"]

nets:
  5V: E1.5V, Mod1.Vin
  N1: E1.GND#1, Mod1.-
  N2: E1.GPIO_12, Mod1.S

custom parts:
  KY-015 Temperature & Humidity Sensor Module: KY-015 temperature and humidity sensor module, provides a low-latency serial interface to measure humidity and temperature.
